# Fritzing sketch stepper_motor_wiring (saved by Fritzing 0.9.3b)

parts:
  Part3 = EasyDriver_v44
  M2 = Stepper Motor - Bipolar
  M3 = Stepper Motor - Bipolar
  Part4 = Photon

nets:
  GND: Part3.GND, Part4.GND
  N1: Part3.STEP, Part4.D4
  N2: Part3.DIR, Part4.D3
  N3: Part3.OUT2A, M2.A, M3.A
  N4: Part3.OUT2B, M2.C, M3.C
  N5: Part3.OUT1A, M2.B, M3.B
  N6: Part3.OUT1B, M2.D, M3.D
  N7: Part3.MS1, Part4.D5
  N8: Part3.ENABLE, Part4.D2
  N9: Part3.MS2, Part4.D6

notes:
  This should be the Big Easy Driver (BED), not just easydriver but the part does not exist yet (pins are very similar though)s
  This is the color coding for the KNF diaphragm pump
  standard stepper
  MS3
